// Logisim project main.circ as structural Verilog: 2 circuits, main circuit main
module main (
);

  wire ARG_TYPE, CLOCK, undriven;
  wire [1:0] DEST_REG;
  wire [5:0] OP;
  wire [15:0] OPERAND, PC_q, undriven_2;

  Clock clock_1 (.out(CLOCK));
  Counter #(.width(16), .max('hffff), .ongoal("stay")) PC (
    .load(undriven), .D(undriven_2), .Q(PC_q), .clk(CLOCK));  // open: count, carry, clr, preset, down
  ROM #(.addrWidth(16), .dataWidth(25), .Select("low")) Program (.addr(PC_q), .data({DEST_REG, ARG_TYPE, OP, OPERAND}));
  Register #(.width(16), .Select("low")) A ();  // open: D, en, Q, clk, clr
  Register #(.width(16), .Select("low")) B ();  // open: D, en, Q, clk, clr
  Register #(.width(16), .Select("low")) D ();  // open: D, en, Q, clk, clr
  Register #(.width(16), .Select("low")) C ();  // open: D, en, Q, clk, clr
  RAM #(.Select("low")) RAM ();  // open: addr, data, sel, clk, ld, clr

  // Notes on the sheet:
  //   Main architecture
  //   contents of Program (hex, n*v repeats v):
  //   ab11 1122
endmodule

module alu (
  input  [15:0] A,
  input  [15:0] B,
  input  [3:0] ALU_OP,
  input  CARRY_IN,
  output [15:0] OUT,
  output ZF,
  output CF
);

  wire [15:0] adder_1_out, adder_2_out, and_1_out, nand_1_out, negator_1_out, nor_1_out, not_1_out, or_1_out,
       subtractor_1_out, subtractor_2_out, xor_1_out;

  Adder #(.width(16)) adder_1 (.a(A), .b(B), .out(adder_1_out));  // open: cin, cout
  Adder #(.width(16)) adder_2 (.a(A), .b(B), .out(adder_2_out), .cin(CARRY_IN));  // open: cout
  Subtractor #(.width(16)) subtractor_1 (.a(A), .b(B), .out(subtractor_1_out));  // open: bin, bout
  Subtractor #(.width(16)) subtractor_2 (.a(A), .b(B), .out(subtractor_2_out), .bin(CARRY_IN));  // open: bout
  Comparator #(.width(16)) comparator_1 (.a(A), .b(B), .eq(ZF), .lt(CF));  // open: gt
  Negator #(.width(16)) negator_1 (.in(A), .out(negator_1_out));
  assign not_1_out = ~A;  // NOT_Gate not_1, 16 bits wide
  assign and_1_out = A & B;  // AND_Gate and_1, 16 bits wide
  assign or_1_out = A | B;  // OR_Gate or_1, 16 bits wide
  assign nand_1_out = ~(A & B);  // NAND_Gate nand_1, 16 bits wide
  assign nor_1_out = ~(A | B);  // NOR_Gate nor_1, 16 bits wide
  assign xor_1_out = A ^ B;  // XOR_Gate xor_1, 16 bits wide
  Multiplexer #(.select(4), .width(16), .enable("false")) multiplexer_1 (
    .in0(adder_1_out), .in1(adder_2_out), .in2(subtractor_1_out), .in3(subtractor_2_out),
    .in4(negator_1_out), .in5(not_1_out), .in6(and_1_out), .in7(or_1_out), .in8(nand_1_out), .in9(nor_1_out),
    .in10(xor_1_out), .out(OUT), .sel(ALU_OP));  // open: in11, in12, in13, in14, in15

  // Notes on the sheet:
  //   ALU interface
endmodule
